# Fritzing sketch drawbot_mint_wiring (saved by Fritzing 0.9.3b)

parts:
  U1 = USB_AB [package=usb-ab-micro-smd]  # not connected
  J5 = Dagu DGServo 9g header (male) [package=THT]
  Servo_Motor_(for_pen_lift) = Basic Servo
  MOTOR1 = 28BYJ-48 Stepper Motor  # not connected
  MOTOR2 = 28BYJ-48 Stepper Motor  # not connected
  BREAKOUT1 = ULN2003A breakout board  # not connected
  BREAKOUT2 = ULN2003A breakout board  # not connected
  MCU1 = Raspberry Pi Zero  # not connected

nets:
  GND: J5.gnd, Servo_Motor_(for_pen_lift).gnd
  VCC: J5.Vcc, Servo_Motor_(for_pen_lift).vcc

notes:
  Wiring for motors can vary a lot, so test connections and don't trust this diagram!

custom parts:
  ULN2003A breakout board: ULN2003A 7-way Darlington Transistor Driver on breakoutboard
